# Fritzing sketch Lab 4 (saved by Fritzing 0.9.9b)
breadboards: 1

parts:
  Tri-Colour_LED = RGB LED (com. cathode, rgb) [package="5 mm [THT]"]
  Resistor_(Green) = Resistor [tolerance=±5% resistance=220 package="2512 [SMD]"]
  Resistor_(Blue) = Resistor [tolerance=±5% resistance=220 package="2512 [SMD]"]
  Resistor_(Red) = Resistor [tolerance=±5% resistance=220 package="2512 [SMD]"]
  Teensy_3_2 = Teensy 3.2  # not connected
  S1 = Momentary Switch [package=ksa_sealed_tac_switch]
  S2 = Momentary Switch [package=ksa_sealed_tac_switch]
  R1 = Resistor [tolerance=±5% power=0.25 resistance=220 package=THT]

nets:
  N1: Tri-Colour_LED.red_anode, Resistor_(Green).Pin_0
  N2: Tri-Colour_LED.common_cathode, S1.1, S2.1
  N3: Tri-Colour_LED.green_anode, Resistor_(Blue).Pin_0
  N4: Tri-Colour_LED.blue_anode, Resistor_(Red).Pin_0
  N5: S1.3, R1.Pin_1

notes:
  CST8227 – Interfacing
  Lab 04 – Pushbuttons to Control LED Colors
  Control a tri-color RGB with two switches and a pull-up resistor.
  Akhond Sarah Mesbah (041009466)

custom parts:
  Teensy 3.2: The Teensy is a complete USB-based microcontoller development system, in a very small footprint, capable of implementing many types of projects. All programming is done via the USB port. No special programmer is needed, only a standard micro-USB cable and a PC or Macintosh with a USB port. It has a USB keyboard/mouse/joystick emulation stack and can be programmed through Arduino IDE.
